// Logisim project basic_pipeline_v2.circ as structural Verilog: 21 circuits, main circuit main
module main (
  input  Reset,
  input  Enable,
  output [19:0] Instruction,
  output [19:0] Instruction_2,
  output [7:0] out_5,
  output [19:0] Instruction_3,
  output [19:0] Instruction_4,
  output [7:0] out_8,
  output [19:0] Instruction_5,
  output [19:0] Instruction_6,
  output OVERFLOW,
  output [19:0] Instruction_7,
  output [19:0] Instruction_8,
  output [2:0] debug,
  output [7:0] out_15,
  output [19:0] Instruction_9,
  output [3:0] debug_2,
  output [7:0] out_18
);

  wire A0, A1, alu_8_by_art_2_p4, ALU_Src_EX, ALU_Src_ID, ALU_Src_MEM, ALU_Src_WB, and_1_out, and_4_out,
       and_5_out, and_6_out, and_7_out, B0, B1, BEQ_EX, BEQ_ID, BEQ_MEM, BEQ_WB, BNEQ_EX, BNEQ_ID, BNEQ_MEM,
       BNEQ_WB, BRANCH_EX, BRANCH_ID, BRANCH_ID_REFINED, BRANCH_MEM, BRANCH_STALL, C0, C1, Clock,
       comparator_1_eq, comparator_2_eq, D0, D1, DR_EX, DR_MEM, DR_WB, DW_EX, DW_MEM, DW_WB, JUMP_EX,
       JUMP_ID_REFINED, JUMP_MEM, JUMP_WB, LW_Hazard, MEM_DATA_FLAG, MEM_SRC_EX, MEM_SRC_MEM, MEM_SRC_WB,
       MEM_to_REG_EX, MEM_to_REG_MEM, MEM_to_REG_WB, MR_ID, MW_ID, not_1_out, not_2_out, not_3_out,
       not_4_out, not_5_out, or_1_out, or_2_out, or_3_out, or_5_out, or_6_out, or_7_out, or_8_out, or_9_out,
       or_10_out, PAST_BRANCH_STALL, PAST_LW_Hazard, PAST_STALL, PREMATURE_JUMP, REG_1_FLAG, REG_2_FLAG,
       REG_DST_EX, REG_DST_MEM, REG_DST_WB, register_1_q, RW_EX, RW_MEM, RW_WB, SHIFT_EX, SHIFT_MEM,
       SHIFT_WB, SR_EX, SR_MEM, SR_WB, STALL, SW_EX, SW_MEM, SW_WB;
  wire [2:0] ALU_OPcode_ID, ALU_OPcode_MEM, ALU_OPcode_WB;
  wire [3:0] bit_splitter_1_shift_amount, OPCODE_ID, REG_RD_EX, REG_RD_ID, REG_RD_MEM, REG_RD_WB, REG_RS_EX,
       REG_RS_MEM, REG_RS_WB, REG_RT_EX, REG_RT_ID, REG_RT_MEM, REG_RT_WB, WRITE_REG_EX, WRITE_REG_MEM,
       WRITE_REG_WB;
  wire [7:0] Alu_A, Alu_B, ALU_OUT_MEM, ALU_OUT_WB, CURR_PC, DATA_1_EX, DATA_1_ID, DATA_1_MEM,
       DATA_1_REVISED_EX, DATA_1_REVISED_ID, DATA_1_WB, DATA_2_EX, DATA_2_ID, DATA_2_MEM, DATA_2_REVISED_EX,
       DATA_2_REVISED_ID, DATA_2_WB, IMMIDIATE_EX, IMMIDIATE_ID, IMMIDIATE_MEM, JUMP_ADDR_EX, JUMP_ADDR_ID,
       JUMP_ADDR_MEM, MEM_DATA_REVISED, multiplexer_3_out, multiplexer_5_out, multiplexer_6_out,
       multiplexer_7_out, multiplexer_9_out, multiplexer_10_out, multiplexer_13_out, multiplexer_14_out,
       multiplexer_18_out, PC, PC_EX, PC_ID, PC_IF, PC_MEM, REG_WRITE_DATA_MEM, REG_WRITE_DATA_MEM_REVISED,
       REG_WRITE_DATA_WB, SHAMT_EX, SHAMT_ID;
  wire [13:3] CONTROL_ID;
  wire [15:0] CONTROL_EX, CONTROL_MEM, CONTROL_REFINED_ID, CONTROL_WB;

  Clock u_Clock (.out(Clock));
  // ALU_8_by_ART alu_8_by_art_1: pin names not known; wires that end beside it: 8'h1, CURR_PC, 3'b000, PC_IF
  Instruction_Memory instruction_memory_1 (
    .PC(PC), .Clock(Clock), .Reset(Reset), .PC_address_Instruction(Instruction_7), .PC_address(CURR_PC));
  and and_1 (and_1_out, Enable, not_1_out);
  not not_1 (not_1_out, STALL);
  IF_ID if_id_1 (
    .PC_IN(PC_IF), .INSTR_IN(Instruction_7), .EN(and_1_out), .CLK(Clock), .CLR(Reset), .PC_OUT(PC_ID),
    .INSTR_OUT(Instruction));
  Register #(.width(1)) register_1 (.D(1'b1), .Q(register_1_q), .clk(Clock), .clr(Reset));  // open: en
  and and_2 (CONTROL_ID[12], register_1_q, PREMATURE_JUMP);
  Bit_Splitter bit_splitter_1 (
    ._20bits_Instruction(Instruction), .Shift_Amount(bit_splitter_1_shift_amount), .Dst_Reg(REG_RD_ID),
    .Src_Reg2(REG_RT_ID), .Src_Reg1(debug_2), .Instruction_Opcode(OPCODE_ID),
    .Address_Immediate(IMMIDIATE_ID), .Target_Jump_Address(JUMP_ADDR_ID));
  assign SHAMT_ID = {{4{1'b0}}, bit_splitter_1_shift_amount};  // Bit_Extender bit_extender_1
  Control_Unit control_unit_1 (
    .Instruction_Opcode(OPCODE_ID), .Shift(CONTROL_ID[3]), .ALU_Op(ALU_OPcode_ID), .Reg_Des(CONTROL_ID[4]),
    .ALU_Src(ALU_Src_ID), .MemToReg(CONTROL_ID[6]), .Reg_Write(CONTROL_ID[13]), .beq(BEQ_ID), .bneq(BNEQ_ID),
    .Mem_write(MW_ID), .Mem_Read(MR_ID), .Jump(PREMATURE_JUMP));
  or or_1 (or_1_out, DR_MEM, SR_MEM);
  or or_2 (or_2_out, DR_EX, SR_EX);
  and and_3 (JUMP_ID_REFINED, CONTROL_ID[12], not_2_out);
  not not_2 (not_2_out, PAST_STALL);
  and and_4 (and_4_out, not_2_out, BRANCH_ID);
  not not_3 (not_3_out, BRANCH_STALL);
  or or_3 (or_3_out, BNEQ_ID, BEQ_ID);
  Register #(.width(1)) register_2 (.D(STALL), .en(1'b1), .Q(PAST_STALL), .clk(Clock), .clr(Reset));
  Register #(.width(1)) register_3 (.D(BRANCH_STALL), .en(1'b1), .Q(PAST_BRANCH_STALL), .clk(Clock), .clr(Reset));
  Multiplexer #(.enable("false")) multiplexer_1 (
    .in0(and_4_out), .in1(BRANCH_ID), .out(BRANCH_ID_REFINED), .sel(and_5_out));
  and and_5 (and_5_out, not_3_out, PAST_BRANCH_STALL);
  BRANCH_STALL branch_stall_1 (
    .MEM_WB_WRITE_REG(WRITE_REG_MEM), .MEM_WB_MR_BIT(or_1_out), .EX_MEM_WRITE_BIT(RW_EX),
    .EX_MEM_MR_BIT(or_2_out), .EX_MEM_WRITE_REG(WRITE_REG_EX), .REGISTER_1_IN(debug_2),
    .REGISTER_2_IN(REG_RT_ID), .BRANCH_STALL(BRANCH_STALL), .IsBranching(or_3_out));
  or or_4 (STALL, LW_Hazard, BRANCH_ID_REFINED, PAST_BRANCH_STALL, JUMP_ID_REFINED, BRANCH_STALL);
  Stack_Op_selector stack_op_selector_1 (
    .src1_reg(debug_2), .Mem_Read(MR_ID), .Mem_Write(MW_ID), .Mem_Out_Selector(CONTROL_ID[7]),
    .Stack_Read(CONTROL_ID[10]), .Data_Read(CONTROL_ID[8]), .Stack_Write(CONTROL_ID[11]),
    .Data_Write(CONTROL_ID[9]));
  Registers registers_1 (
    .Reset(Reset), .Src_Reg1(debug_2), .Clock(Clock), .Reg_Write(RW_WB), .Dst_Reg(WRITE_REG_WB),
    .Write_Data(REG_WRITE_DATA_WB), .Src_Reg2(REG_RT_ID), .DataB(DATA_2_ID), .DataA(DATA_1_ID));
  not not_4 (not_4_out, PAST_LW_Hazard);
  and and_6 (and_6_out, not_4_out, PAST_STALL);
  Multiplexer #(.enable("false")) multiplexer_2 (.in0(BNEQ_ID), .in1(BEQ_ID), .out(BRANCH_ID), .sel(comparator_1_eq));
  Comparator comparator_1 (.a(DATA_1_REVISED_ID), .b(DATA_2_REVISED_ID), .eq(comparator_1_eq));  // open: gt, lt
  RAAAW_HAZARD raaaw_hazard_1 (
    .REGISTER_2(REG_RT_ID), .REG_1_FLAG(REG_1_FLAG), .REGISTER_LOAD(WRITE_REG_WB), .REG_WRITE_BIT(RW_WB),
    .REG_2_FLAG(REG_2_FLAG), .REGISTER_1(debug_2));
  or or_5 (or_5_out, STALL, and_6_out);
  Multiplexer #(.width(8), .enable("false")) multiplexer_3 (
    .in0(PC_IF), .in1(IMMIDIATE_ID), .out(multiplexer_3_out), .sel(BRANCH_ID_REFINED));
  Multiplexer #(.width(16), .disabled(0), .enable("false")) multiplexer_4 (
    .in0({BNEQ_ID, BEQ_ID, CONTROL_ID[13:6], ALU_Src_ID, CONTROL_ID[4:3], ALU_OPcode_ID}), .in1({16{1'b0}}),
    .out(CONTROL_REFINED_ID), .sel(or_5_out));
  Multiplexer #(.width(8), .enable("false")) multiplexer_5 (
    .in0(multiplexer_3_out), .in1(JUMP_ADDR_ID), .out(multiplexer_5_out), .sel(JUMP_ID_REFINED));
  Forwarding_Unit forwarding_unit_1 (
    .ID_EX_Src_Reg_1(debug_2), .EX_Mem_Reg_Write(RW_MEM), .EX_Mem_Des_Reg(WRITE_REG_MEM),
    .Mem_WB_Des_Reg(WRITE_REG_WB), .Mem_WB_Reg_Write(RW_WB), .ID_EX_Src_Reg_2(REG_RT_ID), .Forward_A1(C1),
    .Forward_A0(C0), .Forward_B1(D1), .Forward_B0(D0));
  or or_6 (or_6_out, BNEQ_ID, BEQ_ID);
  Multiplexer #(.width(8), .disabled(0), .enable("false")) multiplexer_6 (
    .in0(DATA_1_ID), .in1(REG_WRITE_DATA_WB), .out(multiplexer_6_out), .sel(REG_1_FLAG));
  Multiplexer #(.width(8), .disabled(0), .enable("false")) multiplexer_7 (
    .in0(DATA_2_ID), .in1(REG_WRITE_DATA_WB), .out(multiplexer_7_out), .sel(REG_2_FLAG));
  or or_7 (or_7_out, CONTROL_ID[9], CONTROL_ID[11]);
  or or_8 (or_8_out, DR_EX, SR_EX);
  Hazard_Detection_Unit hazard_detection_unit_1 (
    .ID_EX_MR(or_8_out), .IF_ID_rs(debug_2), .ID_EX_rt(REG_RT_EX), .IF_ID_rt(REG_RT_ID),
    .LW_Hazard(LW_Hazard), .Load_Store(or_7_out));
  Multiplexer #(.width(8), .enable("false")) multiplexer_8 (
    .in0(multiplexer_5_out), .in1(PC_ID), .out(PC), .sel(or_9_out));
  or or_9 (or_9_out, LW_Hazard, and_7_out, BRANCH_STALL);
  Register #(.width(1)) register_4 (.D(LW_Hazard), .en(1'b1), .Q(PAST_LW_Hazard), .clk(Clock), .clr(Reset));
  or or_10 (or_10_out, BEQ_ID, BNEQ_ID);
  and and_7 (and_7_out, or_10_out, not_5_out);
  not not_5 (not_5_out, BRANCH_ID);
  Multiplexer #(.width(8), .disabled(0), .enable("false")) multiplexer_9 (
    .in0(multiplexer_6_out), .in1(ALU_OUT_MEM), .out(multiplexer_9_out), .sel(C1));
  Multiplexer #(.width(8), .disabled(0), .enable("false")) multiplexer_10 (
    .in0(multiplexer_7_out), .in1(ALU_OUT_MEM), .out(multiplexer_10_out), .sel(D1));
  Multiplexer #(.width(8), .disabled(0), .enable("false")) multiplexer_11 (
    .in0(multiplexer_9_out), .in1(REG_WRITE_DATA_WB), .out(DATA_1_REVISED_ID), .sel(C0));
  Multiplexer #(.width(8), .disabled(0), .enable("false")) multiplexer_12 (
    .in0(multiplexer_10_out), .in1(REG_WRITE_DATA_WB), .out(DATA_2_REVISED_ID), .sel(D0));
  ID_EX id_ex_1 (
    .PC_IN(PC_ID), .CONTROL_IN(CONTROL_REFINED_ID), .DATA_1_IN(DATA_1_REVISED_ID),
    .DATA_2_IN(DATA_2_REVISED_ID), .REG_RS_IN(debug_2), .REG_RT_IN(REG_RT_ID), .REG_RD_IN(REG_RD_ID),
    .IMMD_IN(IMMIDIATE_ID), .SHAMT_IN(SHAMT_ID), .PC_OUT(PC_EX), .CONTROL_OUT(CONTROL_EX),
    .DATA_1_OUT(DATA_1_EX), .DATA_2_OUT(DATA_2_EX), .REG_RS_OUT(REG_RS_EX), .REG_RT_OUT(REG_RT_EX),
    .REG_RD_OUT(REG_RD_EX), .IMMD_OUT(IMMIDIATE_EX), .SHAMT_OUT(SHAMT_EX), .Enable_operation(Enable),
    .CLK(Clock), .CLR(Reset), .JUMP_IN(JUMP_ADDR_ID), .JUMP_OUT(JUMP_ADDR_EX), .INSTR_IN(Instruction),
    .INSTR_OUT(Instruction_2));
  Control_Decoder control_decoder_1 (
    .ALU_OPcode(debug), .SHIFT(SHIFT_EX), .REG_DST(REG_DST_EX), .ALU_Src(ALU_Src_EX),
    .MEM_to_REG(MEM_to_REG_EX), .MEM_SRC(MEM_SRC_EX), .DR(DR_EX), .DW(DW_EX), .SR(SR_EX), .SW(SW_EX),
    .JUMP(JUMP_EX), .RW(RW_EX), .BEQ(BEQ_EX), .BNEQ(BNEQ_EX), .CONTROL_IN(CONTROL_EX));
  Multiplexer #(.width(8), .disabled(0), .enable("false")) multiplexer_13 (
    .in0(DATA_1_EX), .in1(ALU_OUT_MEM), .out(multiplexer_13_out), .sel(A1));
  Multiplexer #(.width(8), .disabled(0), .enable("false")) multiplexer_14 (
    .in0(DATA_2_EX), .in1(ALU_OUT_MEM), .out(multiplexer_14_out), .sel(B1));
  Multiplexer #(.width(8), .disabled(0), .enable("false")) multiplexer_15 (
    .in0(multiplexer_13_out), .in1(REG_WRITE_DATA_WB), .out(DATA_1_REVISED_EX), .sel(A0));
  Multiplexer #(.width(8), .disabled(0), .enable("false")) multiplexer_16 (
    .in0(multiplexer_14_out), .in1(REG_WRITE_DATA_WB), .out(DATA_2_REVISED_EX), .sel(B0));
  Multiplexer #(.width(4), .enable("false")) multiplexer_17 (
    .in0(REG_RT_EX), .in1(REG_RD_EX), .out(WRITE_REG_EX), .sel(REG_DST_EX));
  Multiplexer #(.width(8), .enable("false")) multiplexer_18 (
    .in0(DATA_2_REVISED_EX), .in1(IMMIDIATE_EX), .out(multiplexer_18_out), .sel(ALU_Src_EX));
  Multiplexer #(.width(8), .disabled(0), .enable("false")) multiplexer_19 (
    .in0(DATA_1_REVISED_EX), .in1(SHAMT_EX), .out(Alu_A), .sel(SHIFT_EX));
  Multiplexer #(.width(8), .disabled(0), .enable("false")) multiplexer_20 (
    .in0(multiplexer_18_out), .in1(DATA_1_REVISED_EX), .out(Alu_B), .sel(SHIFT_EX));
  Multiplexer #(.enable("false")) multiplexer_21 (
    .in0(BNEQ_EX), .in1(BEQ_EX), .out(BRANCH_EX), .sel(alu_8_by_art_2_p4));
  // ALU_8_by_ART alu_8_by_art_2: pin names not known; wires that end beside it: Alu_A, Alu_B, debug, alu_8_by_art_2_p4, out_5, OVERFLOW
  Forwarding_Unit forwarding_unit_2 (
    .ID_EX_Src_Reg_1(REG_RS_EX), .EX_Mem_Reg_Write(RW_MEM), .EX_Mem_Des_Reg(WRITE_REG_MEM),
    .Mem_WB_Des_Reg(WRITE_REG_WB), .Mem_WB_Reg_Write(RW_WB), .ID_EX_Src_Reg_2(REG_RT_EX), .Forward_A1(A1),
    .Forward_A0(A0), .Forward_B1(B1), .Forward_B0(B0));
  EX_MEM ex_mem_1 (
    .PC_IN(PC_EX), .CONTROL_IN(CONTROL_EX), .DATA_1_IN(DATA_1_REVISED_EX), .DATA_2_IN(DATA_2_REVISED_EX),
    .REG_RS_IN(REG_RS_EX), .REG_RT_IN(REG_RT_EX), .REG_RD_IN(REG_RD_EX), .PC_OUT(PC_MEM),
    .CONTROL_OUT(CONTROL_MEM), .DATA_1_OUT(DATA_1_MEM), .DATA_2_OUT(DATA_2_MEM), .REG_RS_OUT(REG_RS_MEM),
    .REG_RT_OUT(REG_RT_MEM), .REG_RD_OUT(REG_RD_MEM), .Enable_operation(Enable), .CLK(Clock), .CLR(Reset),
    .ALU_OUT_IN(out_5), .ALU_OUT_OUT(ALU_OUT_MEM), .WRITE_REG_IN(WRITE_REG_EX),
    .WRITE_REG_OUT(WRITE_REG_MEM), .BRANCH_IN(BRANCH_EX), .BRANCH_OUT(BRANCH_MEM), .IMMD_IN(IMMIDIATE_EX),
    .IMMD_OUT(IMMIDIATE_MEM), .JUMP_IN(JUMP_ADDR_EX), .JUMP_OUT(JUMP_ADDR_MEM), .INSTR_IN(Instruction_2),
    .INSTR_OUT(Instruction_3));
  Control_Decoder control_decoder_2 (
    .ALU_OPcode(ALU_OPcode_MEM), .SHIFT(SHIFT_MEM), .REG_DST(REG_DST_MEM), .ALU_Src(ALU_Src_MEM),
    .MEM_to_REG(MEM_to_REG_MEM), .MEM_SRC(MEM_SRC_MEM), .DR(DR_MEM), .DW(DW_MEM), .SR(SR_MEM), .SW(SW_MEM),
    .JUMP(JUMP_MEM), .RW(RW_MEM), .BEQ(BEQ_MEM), .BNEQ(BNEQ_MEM), .CONTROL_IN(CONTROL_MEM));
  LOAD_STORE_HAZARD load_store_hazard_1 (
    .REGISTER_RT(REG_RT_MEM), .REGISTER_LOAD(WRITE_REG_WB), .REG_WRITE_BIT(RW_WB),
    .DATA_STORE_FLAG(MEM_DATA_FLAG), .MEM_READ_BIT(1'b1));
  Stack_Memory stack_memory_1 (
    .Address(ALU_OUT_MEM), .Write_Data(MEM_DATA_REVISED), .Clear(Reset), .Clock(Clock), .Data(out_8),
    .Mem_Write(SW_MEM), .Mem_Read(SR_MEM));
  Data_Memory data_memory_1 (
    .Address(ALU_OUT_MEM), .Write_Data(MEM_DATA_REVISED), .Mem_Write(DW_MEM), .CLK(Clock), .Mem_Read(DR_MEM),
    .in_6(Reset), .Output_data(out_18));
  Multiplexer #(.width(8), .enable("false")) multiplexer_22 (
    .in0(ALU_OUT_MEM), .in1(out_15), .out(REG_WRITE_DATA_MEM), .sel(MEM_to_REG_MEM));
  Multiplexer #(.width(8), .enable("false")) multiplexer_23 (
    .in0(DATA_2_MEM), .in1(REG_WRITE_DATA_WB), .out(MEM_DATA_REVISED), .sel(MEM_DATA_FLAG));
  Multiplexer #(.width(8), .enable("false")) multiplexer_24 (
    .in0(out_18), .in1(out_8), .out(out_15), .sel(MEM_SRC_MEM));
  Comparator #(.width(4)) comparator_2 (.a(REG_RT_MEM), .b(WRITE_REG_MEM), .eq(comparator_2_eq));  // open: gt, lt
  Multiplexer #(.width(8), .enable("false")) multiplexer_25 (
    .in0(ALU_OUT_MEM), .in1(DATA_2_MEM), .out(REG_WRITE_DATA_MEM_REVISED), .sel(comparator_2_eq));
  MEM_WB mem_wb_1 (
    .CONTROL_IN(CONTROL_MEM), .DATA_1_IN(DATA_1_MEM), .DATA_2_IN(DATA_2_MEM), .REG_RS_IN(REG_RS_MEM),
    .REG_RT_IN(REG_RT_MEM), .REG_RD_IN(REG_RD_MEM), .ALU_OUT_IN(ALU_OUT_MEM), .WRITE_REG_IN(WRITE_REG_MEM),
    .REG_WRITE_DATA_IN(REG_WRITE_DATA_MEM), .CONTROL_OUT(CONTROL_WB), .DATA_1_OUT(DATA_1_WB),
    .DATA_2_OUT(DATA_2_WB), .REG_RS_OUT(REG_RS_WB), .REG_RT_OUT(REG_RT_WB), .REG_RD_OUT(REG_RD_WB),
    .ALU_OUT_OUT(ALU_OUT_WB), .WRITE_REG_OUT(WRITE_REG_WB), .REG_WRITE_DATA_OUT(REG_WRITE_DATA_WB),
    .Enable_operation(Enable), .CLK(Clock), .CLR(Reset), .INSTR_IN(Instruction_3), .INSTR_OUT(Instruction_4));  // open: PC_IN, PC_OUT
  Control_Decoder control_decoder_3 (
    .ALU_OPcode(ALU_OPcode_WB), .SHIFT(SHIFT_WB), .REG_DST(REG_DST_WB), .ALU_Src(ALU_Src_WB),
    .MEM_to_REG(MEM_to_REG_WB), .MEM_SRC(MEM_SRC_WB), .DR(DR_WB), .DW(DW_WB), .SR(SR_WB), .SW(SW_WB),
    .JUMP(JUMP_WB), .RW(RW_WB), .BEQ(BEQ_WB), .BNEQ(BNEQ_WB), .CONTROL_IN(CONTROL_WB));

  assign Instruction_5 = Instruction_2;
  assign Instruction_6 = Instruction_3;
  assign Instruction_8 = Instruction;
  assign Instruction_9 = Instruction_7;

  // Other names for the same wires on the sheet: ALU_OPcode_EX[2:0] = debug; ALU_OUT_EX[7:0] = out_5;
  //   CONTROL_ID (some bits) = {BNEQ_ID, BEQ_ID, ALU_Src_ID, ALU_OPcode_ID}; SHIFT_ID = CONTROL_ID[3];
  //   REG_DST_ID = CONTROL_ID[4]; MEM_to_REG_ID = CONTROL_ID[6]; MEM_SRC_ID = CONTROL_ID[7]; DR_ID = CONTROL_ID[8];
  //   DW_ID = CONTROL_ID[9]; SR_ID = CONTROL_ID[10]; SW_ID = CONTROL_ID[11]; JUMP_ID = CONTROL_ID[12];
  //   RW_ID = CONTROL_ID[13]; DATA_OUT[7:0] = out_18; INSTRUCTION_EX[19:0] = Instruction_2;
  //   INSTRUCTION_ID[19:0] = Instruction; INSTRUCTION_IF[19:0] = Instruction_7; INSTRUCTION_MEM[19:0] = Instruction_3;
  //   INSTRUCTION_WB[19:0] = Instruction_4; MEM_OUTPUT[7:0] = out_15; REG_RS_ID[3:0] = debug_2;
  //   STACK_OUT[7:0] = out_8

  // Notes on the sheet:
  //   IF stage
  //   ID stage
  //   EX stage
  //   MEM stage
  //   WB stage
endmodule

// Control Unit
module Control_Unit (
  input  [3:0] Instruction_Opcode,
  output Shift,
  output [2:0] ALU_Op,
  output Reg_Des,
  output ALU_Src,
  output MemToReg,
  output Reg_Write,
  output beq,
  output bneq,
  output Mem_write,
  output Mem_Read,
  output Jump
);

  wire [3:1] rom_1_data;

  ROM #(.addrWidth(4), .dataWidth(16)) rom_1 (
    .addr(Instruction_Opcode),
    .data({Jump, Mem_Read, Mem_write, bneq, beq, Reg_Write, MemToReg, ALU_Src, Reg_Des, ALU_Op, rom_1_data, Shift}),
    .sel(1'b1));

  // Notes on the sheet:
  //   Control Unit
  //   contents of rom_1 (hex, n*v repeats v):
  //   8000 520 2100 4700 4b0 5e1 4a0 480 530 810 5d1 490 500 4c0 1010 510
  //   16bits for which operations need to be done
endmodule

// Data Memory
module Data_Memory (
  input  [7:0] Address,
  input  [7:0] Write_Data,
  input  Mem_Write,
  input  CLK,
  input  Mem_Read,
  input  in_6,
  output [7:0] Output_data
);

  wire not_1_out;

  not not_1 (not_1_out, CLK);
  RAM #(.bus("separate")) ram_1 (
    .addr(Address), .din(Write_Data), .data(Output_data), .str(Mem_Write), .clk(not_1_out), .ld(Mem_Read),
    .clr(in_6));  // open: sel

  // Notes on the sheet:
  //   Hex RAM
endmodule

module Registers (
  input  Reset,
  input  [3:0] Src_Reg1,
  input  Clock,
  input  Reg_Write,
  input  [3:0] Dst_Reg,
  input  [7:0] Write_Data,
  input  [3:0] Src_Reg2,
  output [7:0] DataA,
  output [7:0] DataB
);

  wire decoder_1_out0, decoder_1_out1, decoder_1_out2, decoder_1_out3, decoder_1_out4, decoder_1_out5,
       decoder_1_out6, not_1_out, or_1_out, register_1_q;
  wire [7:0] multiplexer_1_out, sp, t0, t1, t2, t3, t4, zero_q;

  Hex_Digit_Display hex_digit_display_1 (.value(t0[7:4]));  // open: dp
  Decoder #(.select(4), .disabled(0)) decoder_1 (
    .out0(decoder_1_out0), .out1(decoder_1_out1), .out2(decoder_1_out2), .out3(decoder_1_out3),
    .out4(decoder_1_out4), .out5(decoder_1_out5), .out6(decoder_1_out6), .sel(Dst_Reg), .en(Reg_Write));  // open: out7, out8, out9, out10, out11, out12, out13, out14, out15
  Hex_Digit_Display hex_digit_display_2 (.value(t0[3:0]));  // open: dp
  Hex_Digit_Display hex_digit_display_3 (.value(t1[7:4]));  // open: dp
  Hex_Digit_Display hex_digit_display_4 (.value(t1[3:0]));  // open: dp
  Hex_Digit_Display hex_digit_display_5 (.value(t2[7:4]));  // open: dp
  not not_1 (not_1_out, register_1_q);
  Hex_Digit_Display hex_digit_display_6 (.value(t3[7:4]));  // open: dp
  Hex_Digit_Display hex_digit_display_7 (.value(t2[3:0]));  // open: dp
  or or_1 (or_1_out, decoder_1_out6, not_1_out);
  Multiplexer #(.width(8), .enable("false")) multiplexer_1 (
    .in0({8{1'b1}}), .in1(Write_Data), .out(multiplexer_1_out), .sel(register_1_q));
  Register #(.width(1)) register_1 (.D(1'b1), .Q(register_1_q), .clk(Clock), .clr(Reset));  // open: en
  Hex_Digit_Display hex_digit_display_8 (.value(t3[3:0]));  // open: dp
  Register zero (.Q(zero_q), .clr(1'b1));  // open: D, en, clk
  Register u_t0 (.D(Write_Data), .en(decoder_1_out1), .Q(t0), .clk(Clock), .clr(Reset));
  Register u_t1 (.D(Write_Data), .en(decoder_1_out2), .Q(t1), .clk(Clock), .clr(Reset));
  Register u_t2 (.D(Write_Data), .en(decoder_1_out3), .Q(t2), .clk(Clock), .clr(Reset));
  Register u_t3 (.D(Write_Data), .en(decoder_1_out4), .Q(t3), .clk(Clock), .clr(Reset));
  Register u_t4 (.D(Write_Data), .en(decoder_1_out5), .Q(t4), .clk(Clock), .clr(Reset));
  Register u_sp (.D(multiplexer_1_out), .en(or_1_out), .Q(sp), .clk(Clock), .clr(Reset));
  Hex_Digit_Display hex_digit_display_9 (.value(t4[3:0]));  // open: dp
  Hex_Digit_Display hex_digit_display_10 (.value(t4[7:4]));  // open: dp
  Hex_Digit_Display hex_digit_display_11 (.value(sp[7:4]));  // open: dp
  Hex_Digit_Display hex_digit_display_12 (.value(sp[3:0]));  // open: dp
  Multiplexer #(.select(4), .width(8), .enable("false")) multiplexer_2 (
    .in0(zero_q), .in1(t0), .in2(t1), .in3(t2), .in4(t3), .in5(t4), .in6(sp), .out(DataA), .sel(Src_Reg1));  // open: in7, in8, in9, in10, in11, in12, in13, in14, in15
  Multiplexer #(.select(4), .width(8), .enable("false")) multiplexer_3 (
    .in0(zero_q), .in1(t0), .in2(t1), .in3(t2), .in4(t3), .in5(t4), .in6(sp), .out(DataB), .sel(Src_Reg2));  // open: in7, in8, in9, in10, in11, in12, in13, in14, in15
endmodule

// Instruction Memory
module Instruction_Memory (
  input  [7:0] PC,
  input  Clock,
  input  Reset,
  output [7:0] PC_address,
  output [19:0] PC_address_Instruction
);

  Register u_PC (.D(PC), .en(1'b1), .Q(PC_address), .clk(Clock), .clr(Reset));
  ROM #(.dataWidth(20)) rom_1 (.addr(PC_address), .data(PC_address_Instruction), .sel(1'b1));

  // Notes on the sheet:
  //   Instruction memory
  //   reset takes to 0th index
  //   Hex editor storing 20bit inst in ROM
  //   contents of rom_1 (hex, n*v repeats v):
  //   c010a c0201 9210e c0202 9210e c0201 c0301 c0502 72340 70320 70430 c5501 e1508 f00 c0401 26400 f6601
  //   54014 26100 f6601 a1055 26500 f6601 255a2 26500 f6601 352a2 26200 f6601 c2388 26300 f6601 f3481
  //   b4340 26400 f6601 c0146 c0255 41230 26300 f6601 834fe 26400 f6601 c0480 c05aa 64520 26200 f6601
  //   123ff 26300 f6601 3400 3500
endmodule

module ALU_Check (
  input  [7:0] in_1,
  input  [7:0] in_2,
  input  [2:0] in_3,
  output out_4,
  output [7:0] out_5,
  output out_6
);

  // ALU_8_by_ART alu_8_by_art_1: pin names not known; wires that end beside it: in_1, in_2, in_3, out_4, out_5, out_6
endmodule

// Bit Splitter
module Bit_Splitter (
  input  [19:0] _20bits_Instruction,
  output [3:0] Shift_Amount,
  output [3:0] Dst_Reg,
  output [3:0] Src_Reg2,
  output [3:0] Src_Reg1,
  output [3:0] Instruction_Opcode,
  output [7:0] Address_Immediate,
  output [7:0] Target_Jump_Address
);


  assign Address_Immediate = _20bits_Instruction[7:0];
  assign Dst_Reg = _20bits_Instruction[7:4];
  assign Instruction_Opcode = _20bits_Instruction[19:16];
  assign Shift_Amount = _20bits_Instruction[3:0];
  assign Src_Reg1 = _20bits_Instruction[15:12];
  assign Src_Reg2 = _20bits_Instruction[11:8];
  assign Target_Jump_Address = _20bits_Instruction[15:8];
endmodule

// Stack
module Stack_Memory (
  input  [7:0] Address,
  input  [7:0] Write_Data,
  input  Mem_Write,
  input  Mem_Read,
  input  Clear,
  input  Clock,
  output [7:0] Data
);

  wire not_1_out;

  not not_1 (not_1_out, Clock);
  RAM #(.bus("separate")) ram_1 (
    .addr(Address), .din(Write_Data), .data(Data), .str(Mem_Write), .clk(not_1_out), .ld(Mem_Read),
    .clr(Clear));  // open: sel
endmodule

// Sign Extend
module extender (
  input  [3:0] in_1,
  output [7:0] out_2
);

  Multiplexer #(.width(4)) multiplexer_1 (.in0(4'b0000), .in1(4'b1111), .out(out_2[7:4]), .sel(in_1[3]));  // open: en

  assign out_2[3:0] = in_1;
endmodule

module Stack_Op_selector (
  input  [3:0] src1_reg,
  input  Mem_Read,
  input  Mem_Write,
  output Mem_Out_Selector,
  output Stack_Read,
  output Data_Read,
  output Stack_Write,
  output Data_Write
);

  wire not_1_out, not_2_out, not_3_out, not_4_out;

  not not_1 (not_1_out, src1_reg[0]);
  not not_2 (not_2_out, src1_reg[3]);
  and and_1 (Mem_Out_Selector, not_1_out, src1_reg[1], src1_reg[2], not_2_out);
  and and_2 (Stack_Read, Mem_Read, Mem_Out_Selector);
  and and_3 (Stack_Write, Mem_Out_Selector, Mem_Write);
  not not_3 (not_3_out, Stack_Read);
  and and_4 (Data_Read, not_3_out, Mem_Read);
  not not_4 (not_4_out, Stack_Write);
  and and_5 (Data_Write, not_4_out, Mem_Write);
endmodule

module IF_ID (
  input  [7:0] PC_IN,
  input  [19:0] INSTR_IN,
  input  EN,
  input  CLK,
  input  CLR,
  output [7:0] PC_OUT,
  output [19:0] INSTR_OUT
);

  Register register_1 (.D(PC_IN), .en(EN), .Q(PC_OUT), .clk(CLK), .clr(CLR));
  Register #(.width(20)) register_2 (.D(INSTR_IN), .en(EN), .Q(INSTR_OUT), .clk(CLK), .clr(CLR));
endmodule

module ID_EX (
  input  Enable_operation,
  input  [7:0] PC_IN,
  input  [15:0] CONTROL_IN,
  input  [19:0] INSTR_IN,
  input  [7:0] DATA_1_IN,
  input  [7:0] DATA_2_IN,
  input  [3:0] REG_RS_IN,
  input  [3:0] REG_RT_IN,
  input  [3:0] REG_RD_IN,
  input  [7:0] IMMD_IN,
  input  [7:0] JUMP_IN,
  input  [7:0] SHAMT_IN,
  input  CLK,
  input  CLR,
  output [7:0] PC_OUT,
  output [15:0] CONTROL_OUT,
  output [19:0] INSTR_OUT,
  output [7:0] DATA_1_OUT,
  output [7:0] DATA_2_OUT,
  output [3:0] REG_RS_OUT,
  output [3:0] REG_RT_OUT,
  output [3:0] REG_RD_OUT,
  output [7:0] IMMD_OUT,
  output [7:0] JUMP_OUT,
  output [7:0] SHAMT_OUT
);

  Register register_1 (.D(PC_IN), .en(Enable_operation), .Q(PC_OUT), .clk(CLK), .clr(CLR));
  Register #(.width(16)) CONTROL (.D(CONTROL_IN), .en(Enable_operation), .Q(CONTROL_OUT), .clk(CLK), .clr(CLR));
  Register #(.width(20)) register_2 (.D(INSTR_IN), .en(Enable_operation), .Q(INSTR_OUT), .clk(CLK), .clr(CLR));
  Register Data_1 (.D(DATA_1_IN), .en(Enable_operation), .Q(DATA_1_OUT), .clk(CLK), .clr(CLR));
  Register Data_2 (.D(DATA_2_IN), .en(Enable_operation), .Q(DATA_2_OUT), .clk(CLK), .clr(CLR));
  Register #(.width(4)) Src_Reg_1 (.D(REG_RS_IN), .en(Enable_operation), .Q(REG_RS_OUT), .clk(CLK), .clr(CLR));
  Register #(.width(4)) Src_Reg_2 (.D(REG_RT_IN), .en(Enable_operation), .Q(REG_RT_OUT), .clk(CLK), .clr(CLR));
  Register #(.width(4)) Des_Reg (.D(REG_RD_IN), .en(Enable_operation), .Q(REG_RD_OUT), .clk(CLK), .clr(CLR));
  Register Address_Immediate (.D(IMMD_IN), .en(Enable_operation), .Q(IMMD_OUT), .clk(CLK), .clr(CLR));
  Register Jump_Address (.D(JUMP_IN), .en(Enable_operation), .Q(JUMP_OUT), .clk(CLK), .clr(CLR));
  Register Data_2_2 (.D(SHAMT_IN), .en(Enable_operation), .Q(SHAMT_OUT), .clk(CLK), .clr(CLR));
endmodule

// CRTL DECODER
module Control_Decoder (
  input  [15:0] CONTROL_IN,
  output [2:0] ALU_OPcode,
  output SHIFT,
  output REG_DST,
  output ALU_Src,
  output MEM_to_REG,
  output MEM_SRC,
  output DR,
  output DW,
  output SR,
  output SW,
  output JUMP,
  output RW,
  output BEQ,
  output BNEQ
);


  assign ALU_OPcode = CONTROL_IN[2:0];
  assign ALU_Src = CONTROL_IN[5];
  assign BEQ = CONTROL_IN[14];
  assign BNEQ = CONTROL_IN[15];
  assign DR = CONTROL_IN[8];
  assign DW = CONTROL_IN[9];
  assign JUMP = CONTROL_IN[12];
  assign MEM_SRC = CONTROL_IN[7];
  assign MEM_to_REG = CONTROL_IN[6];
  assign REG_DST = CONTROL_IN[4];
  assign RW = CONTROL_IN[13];
  assign SHIFT = CONTROL_IN[3];
  assign SR = CONTROL_IN[10];
  assign SW = CONTROL_IN[11];
endmodule

module EX_MEM (
  input  Enable_operation,
  input  [7:0] PC_IN,
  input  [15:0] CONTROL_IN,
  input  [19:0] INSTR_IN,
  input  BRANCH_IN,
  input  [7:0] DATA_1_IN,
  input  [7:0] DATA_2_IN,
  input  [3:0] REG_RS_IN,
  input  [3:0] REG_RT_IN,
  input  [3:0] REG_RD_IN,
  input  [7:0] ALU_OUT_IN,
  input  [3:0] WRITE_REG_IN,
  input  [7:0] IMMD_IN,
  input  [7:0] JUMP_IN,
  input  CLK,
  input  CLR,
  output [7:0] PC_OUT,
  output [15:0] CONTROL_OUT,
  output [19:0] INSTR_OUT,
  output BRANCH_OUT,
  output [7:0] DATA_1_OUT,
  output [7:0] DATA_2_OUT,
  output [3:0] REG_RS_OUT,
  output [3:0] REG_RT_OUT,
  output [3:0] REG_RD_OUT,
  output [7:0] ALU_OUT_OUT,
  output [3:0] WRITE_REG_OUT,
  output [7:0] IMMD_OUT,
  output [7:0] JUMP_OUT
);

  Register register_1 (.D(PC_IN), .en(Enable_operation), .Q(PC_OUT), .clk(CLK), .clr(CLR));
  Register #(.width(16)) CONTROL (.D(CONTROL_IN), .en(Enable_operation), .Q(CONTROL_OUT), .clk(CLK), .clr(CLR));
  Register #(.width(20)) register_2 (.D(INSTR_IN), .en(Enable_operation), .Q(INSTR_OUT), .clk(CLK), .clr(CLR));
  Register #(.width(1)) CONTROL_2 (.D(BRANCH_IN), .en(Enable_operation), .Q(BRANCH_OUT), .clk(CLK), .clr(CLR));
  Register Data_1 (.D(DATA_1_IN), .en(Enable_operation), .Q(DATA_1_OUT), .clk(CLK), .clr(CLR));
  Register Data_2 (.D(DATA_2_IN), .en(Enable_operation), .Q(DATA_2_OUT), .clk(CLK), .clr(CLR));
  Register #(.width(4)) Src_Reg_1 (.D(REG_RS_IN), .en(Enable_operation), .Q(REG_RS_OUT), .clk(CLK), .clr(CLR));
  Register #(.width(4)) Src_Reg_2 (.D(REG_RT_IN), .en(Enable_operation), .Q(REG_RT_OUT), .clk(CLK), .clr(CLR));
  Register #(.width(4)) Des_Reg (.D(REG_RD_IN), .en(Enable_operation), .Q(REG_RD_OUT), .clk(CLK), .clr(CLR));
  Register ALU_Out (.D(ALU_OUT_IN), .en(Enable_operation), .Q(ALU_OUT_OUT), .clk(CLK), .clr(CLR));
  Register #(.width(4)) Write_Register (
    .D(WRITE_REG_IN), .en(Enable_operation), .Q(WRITE_REG_OUT), .clk(CLK), .clr(CLR));
  Register Address_Immediate (.D(IMMD_IN), .en(Enable_operation), .Q(IMMD_OUT), .clk(CLK), .clr(CLR));
  Register Jump_Address (.D(JUMP_IN), .en(Enable_operation), .Q(JUMP_OUT), .clk(CLK), .clr(CLR));
endmodule

module MEM_WB (
  input  Enable_operation,
  input  [7:0] PC_IN,
  input  [15:0] CONTROL_IN,
  input  [19:0] INSTR_IN,
  input  [7:0] DATA_1_IN,
  input  [7:0] DATA_2_IN,
  input  [3:0] REG_RS_IN,
  input  [3:0] REG_RT_IN,
  input  [3:0] REG_RD_IN,
  input  [7:0] ALU_OUT_IN,
  input  [3:0] WRITE_REG_IN,
  input  [7:0] REG_WRITE_DATA_IN,
  input  CLK,
  input  CLR,
  output [7:0] PC_OUT,
  output [15:0] CONTROL_OUT,
  output [19:0] INSTR_OUT,
  output [7:0] DATA_1_OUT,
  output [7:0] DATA_2_OUT,
  output [3:0] REG_RS_OUT,
  output [3:0] REG_RT_OUT,
  output [3:0] REG_RD_OUT,
  output [7:0] ALU_OUT_OUT,
  output [3:0] WRITE_REG_OUT,
  output [7:0] REG_WRITE_DATA_OUT
);

  Register register_1 (.D(PC_IN), .en(Enable_operation), .Q(PC_OUT), .clk(CLK), .clr(CLR));
  Register #(.width(16)) CONTROL (.D(CONTROL_IN), .en(Enable_operation), .Q(CONTROL_OUT), .clk(CLK), .clr(CLR));
  Register #(.width(20)) register_2 (.D(INSTR_IN), .en(Enable_operation), .Q(INSTR_OUT), .clk(CLK), .clr(CLR));
  Register Data_1 (.D(DATA_1_IN), .en(Enable_operation), .Q(DATA_1_OUT), .clk(CLK), .clr(CLR));
  Register Data_2 (.D(DATA_2_IN), .en(Enable_operation), .Q(DATA_2_OUT), .clk(CLK), .clr(CLR));
  Register #(.width(4)) Src_Reg_1 (.D(REG_RS_IN), .en(Enable_operation), .Q(REG_RS_OUT), .clk(CLK), .clr(CLR));
  Register #(.width(4)) Src_Reg_2 (.D(REG_RT_IN), .en(Enable_operation), .Q(REG_RT_OUT), .clk(CLK), .clr(CLR));
  Register #(.width(4)) Des_Reg (.D(REG_RD_IN), .en(Enable_operation), .Q(REG_RD_OUT), .clk(CLK), .clr(CLR));
  Register ALU_Out (.D(ALU_OUT_IN), .en(Enable_operation), .Q(ALU_OUT_OUT), .clk(CLK), .clr(CLR));
  Register #(.width(4)) Write_Register (
    .D(WRITE_REG_IN), .en(Enable_operation), .Q(WRITE_REG_OUT), .clk(CLK), .clr(CLR));
  Register Register_Write_Data (
    .D(REG_WRITE_DATA_IN), .en(Enable_operation), .Q(REG_WRITE_DATA_OUT), .clk(CLK), .clr(CLR));
endmodule

module Forwarding_Unit (
  input  [3:0] ID_EX_Src_Reg_1,
  input  EX_Mem_Reg_Write,
  input  [3:0] EX_Mem_Des_Reg,
  input  [3:0] Mem_WB_Des_Reg,
  input  Mem_WB_Reg_Write,
  input  [3:0] ID_EX_Src_Reg_2,
  output Forward_A1,
  output Forward_A0,
  output Forward_B1,
  output Forward_B0
);

  wire and_3_out, and_4_out, comparator_1_eq, comparator_2_eq, comparator_3_gt, comparator_4_gt,
       comparator_5_eq, comparator_6_eq, not_1_out, not_2_out;

  Comparator #(.width(4), .mode("unsigned")) comparator_1 (
    .a(Mem_WB_Des_Reg), .b(ID_EX_Src_Reg_1), .eq(comparator_1_eq));  // open: gt, lt
  Comparator #(.width(4), .mode("unsigned")) comparator_2 (
    .a(ID_EX_Src_Reg_1), .b(EX_Mem_Des_Reg), .eq(comparator_2_eq));  // open: gt, lt
  Comparator #(.width(4), .mode("unsigned")) comparator_3 (
    .a(Mem_WB_Des_Reg), .b(4'b0000), .gt(comparator_3_gt));  // open: eq, lt
  Comparator #(.width(4), .mode("unsigned")) comparator_4 (
    .a(EX_Mem_Des_Reg), .b(4'b0000), .gt(comparator_4_gt));  // open: eq, lt
  Comparator #(.width(4), .mode("unsigned")) comparator_5 (
    .a(EX_Mem_Des_Reg), .b(ID_EX_Src_Reg_2), .eq(comparator_5_eq));  // open: gt, lt
  Comparator #(.width(4), .mode("unsigned")) comparator_6 (
    .a(Mem_WB_Des_Reg), .b(ID_EX_Src_Reg_2), .eq(comparator_6_eq));  // open: gt, lt
  and and_1 (Forward_A1, comparator_2_eq, EX_Mem_Reg_Write, comparator_4_gt);
  and and_2 (Forward_B1, EX_Mem_Reg_Write, comparator_4_gt, comparator_5_eq);
  and and_3 (and_3_out, comparator_1_eq, comparator_3_gt, Mem_WB_Reg_Write);
  and and_4 (and_4_out, comparator_3_gt, Mem_WB_Reg_Write, comparator_6_eq);
  not not_1 (not_1_out, Forward_A1);
  and and_5 (Forward_A0, not_1_out, and_3_out);
  not not_2 (not_2_out, Forward_B1);
  and and_6 (Forward_B0, not_2_out, and_4_out);
endmodule

// Hazard Detection
module Hazard_Detection_Unit (
  input  Load_Store,
  input  ID_EX_MR,
  input  [3:0] IF_ID_rs,
  input  [3:0] ID_EX_rt,
  input  [3:0] IF_ID_rt,
  output LW_Hazard
);

  wire comparator_1_eq, comparator_2_eq, not_1_out, or_1_out;

  Comparator #(.width(4), .mode("unsigned")) comparator_1 (
    .a(IF_ID_rs), .b(ID_EX_rt), .eq(comparator_1_eq));  // open: gt, lt
  Comparator #(.width(4), .mode("unsigned")) comparator_2 (
    .a(ID_EX_rt), .b(IF_ID_rt), .eq(comparator_2_eq));  // open: gt, lt
  not not_1 (not_1_out, Load_Store);
  and and_1 (LW_Hazard, ID_EX_MR, not_1_out, or_1_out);
  or or_1 (or_1_out, comparator_1_eq, comparator_2_eq);
endmodule

module RAAAW_HAZARD (
  input  REG_WRITE_BIT,
  input  [3:0] REGISTER_1,
  input  [3:0] REGISTER_LOAD,
  input  [3:0] REGISTER_2,
  output REG_1_FLAG,
  output REG_2_FLAG
);

  wire comparator_1_eq, comparator_2_eq;

  Comparator #(.width(4), .mode("unsigned")) comparator_1 (
    .a(REGISTER_1), .b(REGISTER_LOAD), .eq(comparator_1_eq));  // open: gt, lt
  Comparator #(.width(4), .mode("unsigned")) comparator_2 (
    .a(REGISTER_LOAD), .b(REGISTER_2), .eq(comparator_2_eq));  // open: gt, lt
  and and_1 (REG_1_FLAG, REG_WRITE_BIT, comparator_1_eq);
  and and_2 (REG_2_FLAG, REG_WRITE_BIT, comparator_2_eq);
endmodule

module LOAD_STORE_HAZARD (
  input  [3:0] REGISTER_RT,
  input  [3:0] REGISTER_LOAD,
  input  REG_WRITE_BIT,
  input  MEM_READ_BIT,
  output DATA_STORE_FLAG
);

  wire comparator_1_eq;

  Comparator #(.width(4), .mode("unsigned")) comparator_1 (
    .a(REGISTER_RT), .b(REGISTER_LOAD), .eq(comparator_1_eq));  // open: gt, lt
  and and_1 (DATA_STORE_FLAG, comparator_1_eq, MEM_READ_BIT, REG_WRITE_BIT);
endmodule

module BRANCH_STALL (
  input  [3:0] REGISTER_1_IN,
  input  [3:0] REGISTER_2_IN,
  input  [3:0] MEM_WB_WRITE_REG,
  input  MEM_WB_MR_BIT,
  input  EX_MEM_WRITE_BIT,
  input  EX_MEM_MR_BIT,
  input  [3:0] EX_MEM_WRITE_REG,
  input  IsBranching,
  output BRANCH_STALL
);

  wire and_1_out, and_2_out, comparator_1_eq, comparator_2_eq, comparator_3_eq, comparator_4_eq,
       comparator_5_eq, comparator_6_eq, not_1_out, not_2_out, or_1_out, or_2_out, or_3_out, or_4_out;

  Comparator #(.width(4)) comparator_1 (.a(MEM_WB_WRITE_REG), .b(4'b0000), .eq(comparator_1_eq));  // open: gt, lt
  Comparator #(.width(4)) comparator_2 (.a(EX_MEM_WRITE_REG), .b(4'b0000), .eq(comparator_2_eq));  // open: gt, lt
  Comparator #(.width(4)) comparator_3 (.a(REGISTER_1_IN), .b(MEM_WB_WRITE_REG), .eq(comparator_3_eq));  // open: gt, lt
  Comparator #(.width(4)) comparator_4 (.a(REGISTER_2_IN), .b(MEM_WB_WRITE_REG), .eq(comparator_4_eq));  // open: gt, lt
  Comparator #(.width(4)) comparator_5 (.a(REGISTER_1_IN), .b(EX_MEM_WRITE_REG), .eq(comparator_5_eq));  // open: gt, lt
  Comparator #(.width(4)) comparator_6 (.a(REGISTER_2_IN), .b(EX_MEM_WRITE_REG), .eq(comparator_6_eq));  // open: gt, lt
  not not_1 (not_1_out, comparator_2_eq);
  or or_1 (or_1_out, comparator_3_eq, comparator_4_eq);
  or or_2 (or_2_out, comparator_5_eq, comparator_6_eq);
  not not_2 (not_2_out, comparator_1_eq);
  or or_3 (or_3_out, EX_MEM_WRITE_BIT, EX_MEM_MR_BIT);
  and and_1 (and_1_out, MEM_WB_MR_BIT, or_1_out, not_2_out);
  and and_2 (and_2_out, or_3_out, or_2_out, not_1_out);
  or or_4 (or_4_out, and_1_out, and_2_out);
  and and_3 (BRANCH_STALL, or_4_out, IsBranching);
endmodule

module BRANCH_FORWARD (
  input  [3:0] REGISTER_1_IN,
  input  [3:0] REGISTER_2_IN,
  input  [3:0] MEM_WB_WRITE_REG,
  input  MEM_WB_MR_BIT,
  input  EX_MEM_WRITE_BIT,
  input  EX_MEM_MR_BIT,
  input  [3:0] EX_MEM_WRITE_REG,
  input  BRANCH,
  output BRANCH_STALL
);

  wire and_1_out, and_2_out, comparator_1_eq, comparator_2_eq, comparator_3_eq, comparator_4_eq,
       comparator_5_eq, comparator_6_eq, not_1_out, not_2_out, or_1_out, or_2_out, or_3_out, or_4_out;

  Comparator #(.width(4)) comparator_1 (.a(MEM_WB_WRITE_REG), .b(4'b0000), .eq(comparator_1_eq));  // open: gt, lt
  Comparator #(.width(4)) comparator_2 (.a(EX_MEM_WRITE_REG), .b(4'b0000), .eq(comparator_2_eq));  // open: gt, lt
  Comparator #(.width(4)) comparator_3 (.a(REGISTER_1_IN), .b(MEM_WB_WRITE_REG), .eq(comparator_3_eq));  // open: gt, lt
  Comparator #(.width(4)) comparator_4 (.a(REGISTER_2_IN), .b(MEM_WB_WRITE_REG), .eq(comparator_4_eq));  // open: gt, lt
  Comparator #(.width(4)) comparator_5 (.a(REGISTER_1_IN), .b(EX_MEM_WRITE_REG), .eq(comparator_5_eq));  // open: gt, lt
  Comparator #(.width(4)) comparator_6 (.a(REGISTER_2_IN), .b(EX_MEM_WRITE_REG), .eq(comparator_6_eq));  // open: gt, lt
  not not_1 (not_1_out, comparator_2_eq);
  or or_1 (or_1_out, comparator_3_eq, comparator_4_eq);
  or or_2 (or_2_out, comparator_5_eq, comparator_6_eq);
  not not_2 (not_2_out, comparator_1_eq);
  or or_3 (or_3_out, EX_MEM_WRITE_BIT, EX_MEM_MR_BIT);
  and and_1 (and_1_out, MEM_WB_MR_BIT, or_1_out, not_2_out);
  and and_2 (and_2_out, or_3_out, or_2_out, not_1_out);
  or or_4 (or_4_out, and_1_out, and_2_out);
  and and_3 (BRANCH_STALL, or_4_out, BRANCH);
endmodule
