// Logisim project single_cycle.circ as structural Verilog: 10 circuits, main circuit main
module main (
  input  Reset,
  output [7:0] out_2,
  output [3:0] debug,
  output [19:0] Instruction,
  output Overflow,
  output [2:0] debug_2,
  output [7:0] out_7,
  output [7:0] debug_3
);

  wire alu_8_by_art_2_p4, ALU_Src, beq, bneq, Branch, Clock, data_read, data_write, Jump, Mem_out_selector,
       Mem_Read, Mem_Write, MemToReg, Reg_Dst, Reg_Write, Shift, St_read, St_write;
  wire [3:0] Dst_Reg, Instruction_Opcode, multiplexer_3_out, Shift_Amount, Src_Reg2;
  wire [7:0] alu_8_by_art_1_p4, Alu_A, Alu_B, ALU_Output, bit_extender_1_out, data_memory_1_output_data,
       DataA, DataB, Immediate, Jump_address, multiplexer_1_out, multiplexer_4_out, PC, PC_address;

  Clock u_Clock (.out(Clock));
  // ALU_8_by_ART alu_8_by_art_1: pin names not known; wires that end beside it: 8'h1, PC_address, 3'b000, alu_8_by_art_1_p4
  Instruction_Memory instruction_memory_1 (
    .PC(PC), .Clock(Clock), .Reset(Reset), .PC_address_Instruction(Instruction), .PC_address(PC_address));
  Multiplexer #(.width(8), .enable("false")) multiplexer_1 (
    .in0(alu_8_by_art_1_p4), .in1(Immediate), .out(multiplexer_1_out), .sel(Branch));
  Bit_Splitter bit_splitter_1 (
    ._20bits_Instruction(Instruction), .Shift_Amount(Shift_Amount), .Dst_Reg(Dst_Reg), .Src_Reg2(Src_Reg2),
    .Src_Reg1(debug), .Instruction_Opcode(Instruction_Opcode), .Address_Immediate(Immediate),
    .Target_Jump_Address(Jump_address));
  Multiplexer #(.width(8), .enable("false")) multiplexer_2 (
    .in0(multiplexer_1_out), .in1(Jump_address), .out(PC), .sel(Jump));
  Multiplexer #(.width(4), .enable("false")) multiplexer_3 (
    .in0(Src_Reg2), .in1(Dst_Reg), .out(multiplexer_3_out), .sel(Reg_Dst));
  Control_Unit control_unit_1 (
    .Instruction_Opcode(Instruction_Opcode), .Shift(Shift), .ALU_Op(debug_2), .Reg_Des(Reg_Dst),
    .ALU_Src(ALU_Src), .MemToReg(MemToReg), .Reg_Write(Reg_Write), .beq(beq), .bneq(bneq),
    .Mem_write(Mem_Write), .Mem_Read(Mem_Read), .Jump(Jump));
  Registers registers_1 (
    .Reset(Reset), .Src_Reg1(debug), .Clock(Clock), .Reg_Write(Reg_Write), .Dst_Reg(multiplexer_3_out),
    .Write_Data(debug_3), .Src_Reg2(Src_Reg2), .DataB(DataB), .DataA(DataA));
  Multiplexer #(.width(8), .enable("false")) multiplexer_4 (
    .in0(DataB), .in1(Immediate), .out(multiplexer_4_out), .sel(ALU_Src));
  assign bit_extender_1_out = {{4{1'b0}}, Shift_Amount};  // Bit_Extender bit_extender_1
  Multiplexer #(.width(8), .disabled(0), .enable("false")) multiplexer_5 (
    .in0(multiplexer_4_out), .in1(DataA), .out(Alu_B), .sel(Shift));
  Multiplexer #(.width(8), .disabled(0), .enable("false")) multiplexer_6 (
    .in0(DataA), .in1(bit_extender_1_out), .out(Alu_A), .sel(Shift));
  // ALU_8_by_ART alu_8_by_art_2: pin names not known; wires that end beside it: Alu_A, Alu_B, debug_2, alu_8_by_art_2_p4, ALU_Output, Overflow
  Multiplexer #(.enable("false")) multiplexer_7 (.in0(bneq), .in1(beq), .out(Branch), .sel(alu_8_by_art_2_p4));
  Stack_Memory stack_memory_1 (
    .Address(ALU_Output), .Write_Data(DataB), .Clear(Reset), .Clock(Clock), .Data(out_2),
    .Mem_Write(St_write), .Mem_Read(St_read));
  Data_Memory data_memory_1 (
    .Address(ALU_Output), .Write_Data(DataB), .Mem_Write(data_write), .CLK(Clock), .Mem_Read(data_read),
    .in_6(Reset), .Output_data(data_memory_1_output_data));
  Stack_Op_selector stack_op_selector_1 (
    .src1_reg(debug), .Mem_Read(Mem_Read), .Mem_Write(Mem_Write), .Mem_Out_Selector(Mem_out_selector),
    .Stack_Read(St_read), .Data_Read(data_read), .Stack_Write(St_write), .Data_Write(data_write));
  Multiplexer #(.width(8), .enable("false")) multiplexer_8 (
    .in0(data_memory_1_output_data), .in1(out_2), .out(out_7), .sel(Mem_out_selector));
  Multiplexer #(.width(8), .enable("false")) multiplexer_9 (
    .in0(ALU_Output), .in1(out_7), .out(debug_3), .sel(MemToReg));

  // Other names for the same wires on the sheet: ALU_Opcode[2:0] = debug_2; Memory_Output[7:0] = out_7;
  //   Src_Reg1[3:0] = debug; stack_out[7:0] = out_2; WriteData[7:0] = debug_3
endmodule

// Control Unit
module Control_Unit (
  input  [3:0] Instruction_Opcode,
  output Shift,
  output [2:0] ALU_Op,
  output Reg_Des,
  output ALU_Src,
  output MemToReg,
  output Reg_Write,
  output beq,
  output bneq,
  output Mem_write,
  output Mem_Read,
  output Jump
);

  wire [3:1] rom_1_data;

  ROM #(.addrWidth(4), .dataWidth(16)) rom_1 (
    .addr(Instruction_Opcode),
    .data({Jump, Mem_Read, Mem_write, bneq, beq, Reg_Write, MemToReg, ALU_Src, Reg_Des, ALU_Op, rom_1_data, Shift}),
    .sel(1'b1));

  // Notes on the sheet:
  //   Control Unit
  //   contents of rom_1 (hex, n*v repeats v):
  //   8000 520 2100 4700 4b0 5e1 4a0 480 530 810 5d1 490 500 4c0 1010 510
  //   16bits for which operations need to be done
endmodule

// Data Memory
module Data_Memory (
  input  [7:0] Address,
  input  [7:0] Write_Data,
  input  Mem_Write,
  input  CLK,
  input  Mem_Read,
  input  in_6,
  output [7:0] Output_data
);

  wire not_1_out;

  not not_1 (not_1_out, CLK);
  RAM #(.bus("separate")) ram_1 (
    .addr(Address), .din(Write_Data), .data(Output_data), .str(Mem_Write), .clk(not_1_out), .ld(Mem_Read),
    .clr(in_6));  // open: sel

  // Notes on the sheet:
  //   Hex RAM
endmodule

// Instruction Memory
module Instruction_Memory (
  input  [7:0] PC,
  input  Clock,
  input  Reset,
  output [7:0] PC_address,
  output [19:0] PC_address_Instruction
);

  Register u_PC (.D(PC), .en(1'b1), .Q(PC_address), .clk(Clock), .clr(Reset));
  ROM #(.dataWidth(20)) rom_1 (.addr(PC_address), .data(PC_address_Instruction), .sel(1'b1));

  // Notes on the sheet:
  //   Instruction memory
  //   reset takes to 0th index
  //   Hex editor storing 20bit inst in ROM
  //   contents of rom_1 (hex, n*v repeats v):
  //   c0105 f1205 71240 94105 1300 a1052 b5420 62150 d5420 82200 12114 22103 32203 52021 1200 262fc 361fc
  //   1300 e120f 1300
endmodule

module ALU_Check (
  input  [7:0] in_1,
  input  [7:0] in_2,
  input  [2:0] in_3,
  output out_4,
  output [7:0] out_5,
  output out_6
);

  // ALU_8_by_ART alu_8_by_art_1: pin names not known; wires that end beside it: in_1, in_2, in_3, out_4, out_5, out_6
endmodule

module Registers (
  input  Reset,
  input  [3:0] Src_Reg1,
  input  Clock,
  input  Reg_Write,
  input  [3:0] Dst_Reg,
  input  [7:0] Write_Data,
  input  [3:0] Src_Reg2,
  output [7:0] DataA,
  output [7:0] DataB
);

  wire decoder_1_out0, decoder_1_out1, decoder_1_out2, decoder_1_out3, decoder_1_out4, decoder_1_out5,
       decoder_1_out6, not_1_out, or_1_out, register_1_q;
  wire [7:0] multiplexer_1_out, sp, t0, t1, t2, t3, t4, zero_q;

  Hex_Digit_Display hex_digit_display_1 (.value(t0[7:4]));  // open: dp
  Decoder #(.select(4), .disabled(0)) decoder_1 (
    .out0(decoder_1_out0), .out1(decoder_1_out1), .out2(decoder_1_out2), .out3(decoder_1_out3),
    .out4(decoder_1_out4), .out5(decoder_1_out5), .out6(decoder_1_out6), .sel(Dst_Reg), .en(Reg_Write));  // open: out7, out8, out9, out10, out11, out12, out13, out14, out15
  Hex_Digit_Display hex_digit_display_2 (.value(t0[3:0]));  // open: dp
  Hex_Digit_Display hex_digit_display_3 (.value(t1[7:4]));  // open: dp
  Hex_Digit_Display hex_digit_display_4 (.value(t1[3:0]));  // open: dp
  Hex_Digit_Display hex_digit_display_5 (.value(t2[7:4]));  // open: dp
  not not_1 (not_1_out, register_1_q);
  Hex_Digit_Display hex_digit_display_6 (.value(t2[3:0]));  // open: dp
  Hex_Digit_Display hex_digit_display_7 (.value(t3[7:4]));  // open: dp
  or or_1 (or_1_out, decoder_1_out6, not_1_out);
  Multiplexer #(.width(8), .enable("false")) multiplexer_1 (
    .in0({8{1'b1}}), .in1(Write_Data), .out(multiplexer_1_out), .sel(register_1_q));
  Register #(.width(1)) register_1 (.D(1'b1), .Q(register_1_q), .clk(Clock), .clr(Reset));  // open: en
  Hex_Digit_Display hex_digit_display_8 (.value(t3[3:0]));  // open: dp
  Register zero (.Q(zero_q), .clr(1'b1));  // open: D, en, clk
  Register u_t0 (.D(Write_Data), .en(decoder_1_out1), .Q(t0), .clk(Clock), .clr(Reset));
  Register u_t1 (.D(Write_Data), .en(decoder_1_out2), .Q(t1), .clk(Clock), .clr(Reset));
  Register u_t2 (.D(Write_Data), .en(decoder_1_out3), .Q(t2), .clk(Clock), .clr(Reset));
  Register u_t3 (.D(Write_Data), .en(decoder_1_out4), .Q(t3), .clk(Clock), .clr(Reset));
  Register u_t4 (.D(Write_Data), .en(decoder_1_out5), .Q(t4), .clk(Clock), .clr(Reset));
  Register u_sp (.D(multiplexer_1_out), .en(or_1_out), .Q(sp), .clk(Clock), .clr(Reset));
  Hex_Digit_Display hex_digit_display_9 (.value(t4[3:0]));  // open: dp
  Hex_Digit_Display hex_digit_display_10 (.value(t4[7:4]));  // open: dp
  Hex_Digit_Display hex_digit_display_11 (.value(sp[7:4]));  // open: dp
  Hex_Digit_Display hex_digit_display_12 (.value(sp[3:0]));  // open: dp
  Multiplexer #(.select(4), .width(8), .enable("false")) multiplexer_2 (
    .in0(zero_q), .in1(t0), .in2(t1), .in3(t2), .in4(t3), .in5(t4), .in6(sp), .out(DataA), .sel(Src_Reg1));  // open: in7, in8, in9, in10, in11, in12, in13, in14, in15
  Multiplexer #(.select(4), .width(8), .enable("false")) multiplexer_3 (
    .in0(zero_q), .in1(t0), .in2(t1), .in3(t2), .in4(t3), .in5(t4), .in6(sp), .out(DataB), .sel(Src_Reg2));  // open: in7, in8, in9, in10, in11, in12, in13, in14, in15
endmodule

// Bit Splitter
module Bit_Splitter (
  input  [19:0] _20bits_Instruction,
  output [3:0] Shift_Amount,
  output [3:0] Dst_Reg,
  output [3:0] Src_Reg2,
  output [3:0] Src_Reg1,
  output [3:0] Instruction_Opcode,
  output [7:0] Address_Immediate,
  output [7:0] Target_Jump_Address
);


  assign Address_Immediate = _20bits_Instruction[7:0];
  assign Dst_Reg = _20bits_Instruction[7:4];
  assign Instruction_Opcode = _20bits_Instruction[19:16];
  assign Shift_Amount = _20bits_Instruction[3:0];
  assign Src_Reg1 = _20bits_Instruction[15:12];
  assign Src_Reg2 = _20bits_Instruction[11:8];
  assign Target_Jump_Address = _20bits_Instruction[15:8];
endmodule

// Stack
module Stack_Memory (
  input  [7:0] Address,
  input  [7:0] Write_Data,
  input  Mem_Write,
  input  Mem_Read,
  input  Clear,
  input  Clock,
  output [7:0] Data
);

  wire not_1_out;

  not not_1 (not_1_out, Clock);
  RAM #(.bus("separate")) ram_1 (
    .addr(Address), .din(Write_Data), .data(Data), .str(Mem_Write), .clk(not_1_out), .ld(Mem_Read),
    .clr(Clear));  // open: sel
endmodule

// Sign Extend
module extender (
  input  [3:0] in_1,
  output [7:0] out_2
);

  Multiplexer #(.width(4)) multiplexer_1 (.in0(4'b0000), .in1(4'b1111), .out(out_2[7:4]), .sel(in_1[3]));  // open: en

  assign out_2[3:0] = in_1;
endmodule

module Stack_Op_selector (
  input  [3:0] src1_reg,
  input  Mem_Read,
  input  Mem_Write,
  output Mem_Out_Selector,
  output Stack_Read,
  output Data_Read,
  output Stack_Write,
  output Data_Write
);

  wire not_1_out, not_2_out, not_3_out, not_4_out;

  not not_1 (not_1_out, src1_reg[0]);
  not not_2 (not_2_out, src1_reg[3]);
  and and_1 (Mem_Out_Selector, not_1_out, src1_reg[1], src1_reg[2], not_2_out);
  and and_2 (Stack_Read, Mem_Read, Mem_Out_Selector);
  and and_3 (Stack_Write, Mem_Out_Selector, Mem_Write);
  not not_3 (not_3_out, Stack_Read);
  and and_4 (Data_Read, not_3_out, Mem_Read);
  not not_4 (not_4_out, Stack_Write);
  and and_5 (Data_Write, not_4_out, Mem_Write);
endmodule
